// Digital circuit part_a.dig as structural Verilog
module part_a (
  input  in_0,
  input  in_1,
  input  in_2,
  output out_0
);

  wire not_1_out, not_2_out, not_3_out, not_4_out, or_1_out, or_2_out, or_3_out, or_4_out;

  not not_1 (not_1_out, in_1);
  or or_1 (or_1_out, not_1_out, not_2_out);
  not not_2 (not_2_out, in_0);
  not not_3 (not_3_out, in_1);
  or or_2 (or_2_out, not_3_out, not_4_out);
  not not_4 (not_4_out, in_2);
  or or_3 (or_3_out, or_1_out, in_2);
  or or_4 (or_4_out, in_0, or_2_out);
  and and_1 (out_0, or_3_out, or_4_out);
endmodule

/* Test case part_a_test:
in_0 in_1 in_2 out_0
 0    0    0    1
 0    0    1    1
 0    1    0    1
 0    1    1    0
 1    0    0    1
 1    0    1    1
 1    1    0    0
 1    1    1    1
*/
