// Digital circuit lab2_part2.dig as structural Verilog
module lab2_part2 (
  input  in0,
  input  in1,
  input  in2,
  input  in3,
  input  in_21,
  input  in_22,
  output seg_a,
  output seg_f,
  output seg_b,
  output seg_g,
  output seg_e,
  output seg_c,
  output seg_d,
  output seg_dp,
  output sign_a,
  output sign_f,
  output sign_b,
  output sign_g,
  output sign_e,
  output sign_c,
  output sign_d,
  output sign_dp
);

  wire and_1_out, and_2_out, and_3_out, and_4_out, and_5_out, and_6_out, and_7_out, and_8_out, and_9_out,
       and_10_out, and_11_out, and_12_out, and_13_out, and_14_out, and_15_out, and_16_out, and_17_out,
       and_18_out, and_19_out, and_20_out, and_21_out, and_22_out, and_23_out, and_24_out, and_25_out,
       and_26_out, and_27_out, and_28_out, and_29_out, and_30_out, and_31_out, and_32_out, and_33_out,
       not_1_out, not_2_out, not_3_out, not_4_out, not_5_out, not_6_out, not_7_out, not_8_out, not_9_out,
       not_10_out, not_11_out, not_12_out, not_13_out, not_14_out, not_15_out, not_16_out, not_17_out,
       not_18_out, not_19_out, not_20_out, not_21_out, not_22_out, not_23_out, not_24_out, not_25_out,
       not_26_out, not_27_out, not_28_out, not_29_out, not_30_out, not_31_out, not_32_out, not_33_out,
       not_34_out, or_1_out, or_2_out, or_3_out, or_4_out, or_5_out, or_6_out, or_7_out, or_8_out, or_12_out,
       or_14_out, or_15_out, or_16_out, or_17_out, or_19_out;

  Seven_Seg seven_seg_1 (.a(in_22), .b(in_22), .c(in_22), .d(in_22), .e(in_22), .f(in_22), .g(in3), .dp(in_22));
  Seven_Seg seven_seg_2 (.a(seg_a), .b(seg_b), .c(seg_c), .d(seg_d), .e(seg_e), .f(seg_f), .g(seg_g), .dp(in_21));
  not not_1 (not_1_out, in3);
  not not_2 (not_2_out, in0);
  not not_3 (not_3_out, in2);
  not not_4 (not_4_out, in0);
  not not_5 (not_5_out, in2);
  and and_1 (and_1_out, in2, in0);
  not not_6 (not_6_out, in1);
  and and_2 (and_2_out, in3, not_7_out);
  not not_7 (not_7_out, in1);
  not not_8 (not_8_out, in2);
  and and_3 (and_3_out, not_8_out, not_9_out);
  not not_9 (not_9_out, in3);
  and and_4 (and_4_out, in2, in3);
  and and_5 (and_5_out, not_10_out, not_11_out);
  not not_10 (not_10_out, in0);
  not not_11 (not_11_out, in1);
  and and_6 (and_6_out, in2, in1);
  or or_1 (or_1_out, not_12_out, in0);
  not not_12 (not_12_out, in1);
  and and_7 (and_7_out, in2, not_13_out);
  not not_13 (not_13_out, in3);
  and and_8 (and_8_out, not_14_out, in3);
  not not_14 (not_14_out, in2);
  and and_9 (and_9_out, in1, not_1_out);
  and and_10 (and_10_out, in1, not_2_out);
  and and_11 (and_11_out, not_3_out, not_4_out);
  and and_12 (and_12_out, in3, not_5_out);
  or or_2 (or_2_out, and_9_out, and_10_out);
  and and_13 (and_13_out, and_1_out, not_6_out);
  or or_3 (or_3_out, and_2_out, and_3_out);
  or or_4 (or_4_out, and_4_out, and_5_out);
  and and_14 (and_14_out, and_6_out, in0);
  or or_5 (or_5_out, or_1_out, and_7_out);
  or or_6 (or_6_out, and_11_out, and_12_out);
  or or_7 (or_7_out, or_2_out, or_6_out);
  or or_8 (or_8_out, or_3_out, or_4_out);
  or or_9 (seg_c, or_5_out, and_8_out);
  or or_10 (seg_a, or_7_out, and_13_out);
  or or_11 (seg_b, or_8_out, and_14_out);
  not not_15 (not_15_out, in0);
  not not_16 (not_16_out, in0);
  not not_17 (not_17_out, in2);
  not not_18 (not_18_out, in1);
  not not_19 (not_19_out, in2);
  not not_20 (not_20_out, in0);
  not not_21 (not_21_out, in0);
  not not_22 (not_22_out, in2);
  not not_23 (not_23_out, in0);
  not not_24 (not_24_out, in1);
  not not_25 (not_25_out, in2);
  not not_26 (not_26_out, in1);
  not not_27 (not_27_out, in3);
  not not_28 (not_28_out, in0);
  not not_29 (not_29_out, in3);
  not not_30 (not_30_out, in0);
  not not_31 (not_31_out, in2);
  not not_32 (not_32_out, in1);
  not not_33 (not_33_out, in0);
  not not_34 (not_34_out, in1);
  and and_15 (and_15_out, in1, not_15_out);
  and and_16 (and_16_out, not_16_out, not_17_out);
  and and_17 (and_17_out, in2, not_18_out);
  and and_18 (and_18_out, not_19_out, in1);
  and and_19 (and_19_out, in1, not_20_out);
  and and_20 (and_20_out, not_21_out, not_22_out);
  and and_21 (and_21_out, not_23_out, not_24_out);
  and and_22 (and_22_out, not_25_out, in1);
  and and_23 (and_23_out, in2, not_26_out);
  and and_24 (and_24_out, in2, not_28_out);
  and and_25 (and_25_out, in1, not_30_out);
  and and_26 (and_26_out, in1, not_31_out);
  and and_27 (and_27_out, in2, not_32_out);
  and and_28 (and_28_out, in3, not_33_out);
  or or_12 (or_12_out, and_15_out, and_16_out);
  and and_29 (and_29_out, and_17_out, in0);
  or or_13 (seg_e, and_19_out, and_20_out);
  and and_30 (and_30_out, and_23_out, not_27_out);
  and and_31 (and_31_out, and_24_out, not_29_out);
  or or_14 (or_14_out, and_25_out, and_26_out);
  and and_32 (and_32_out, and_28_out, not_34_out);
  and and_33 (and_33_out, and_22_out, in3);
  or or_15 (or_15_out, or_12_out, and_29_out);
  or or_16 (or_16_out, and_21_out, and_33_out);
  or or_17 (or_17_out, and_27_out, and_32_out);
  or or_18 (seg_d, or_15_out, and_18_out);
  or or_19 (or_19_out, and_30_out, and_31_out);
  or or_20 (seg_g, or_14_out, or_17_out);
  or or_21 (seg_f, or_16_out, or_19_out);

  assign seg_dp = in_21;
  assign sign_a = in_22;
  assign sign_b = in_22;
  assign sign_c = in_22;
  assign sign_d = in_22;
  assign sign_dp = in_22;
  assign sign_e = in_22;
  assign sign_f = in_22;
  assign sign_g = in3;

  // Notes on the sheet:
  //   Interface (do not edit the content inside this box)
  //   Outputs:
  //   Inputs
  //   Sign
  //   Decimal Number
endmodule

/* Test case:
in3 in2 in1 in0  sign_a sign_b sign_c sign_d sign_e sign_f sign_g  seg_a seg_b seg_c seg_d seg_e seg_f seg_g
 0   0   0   0    0      0      0      0      0      0      0       1     1     1     1     1     1     0
*/
